// Logisim project SAP-1.0.circ as structural Verilog: 6 circuits, main circuit main
module main (
  input  couter_oe,
  input  WE,
  input  [3:0] in_3,
  input  we_2,
  input  [7:0] Testing_data,
  input  OE,
  input  Counter_enable,
  input  in_8,
  input  WE_3,
  input  in_10,
  input  in_11,
  input  OE_2,
  input  OE_3,
  input  WE_4,
  input  OE_internal,
  input  WE_5,
  input  OE_4,
  input  OE_5,
  input  WE_6,
  input  WE_7,
  input  OE_6,
  input  WE_8,
  output [3:0] Content_counter,
  output [3:0] Content,
  output [7:0] out_25,
  output [7:0] out_26,
  output [7:0] out_27,
  output [7:0] A,
  output [7:0] out_29,
  output [7:0] B
);

  wire clock_1_out;
  wire [3:0] controlled_buffer_1_out, decoder_decimal_1_out_2, decoder_decimal_1_out_2_2,
       decoder_decimal_1_out_2_3, decoder_decimal_1_out_2_4, decoder_decimal_1_out_2_5,
       decoder_decimal_1_out_2_6, decoder_decimal_1_out_2_7, decoder_decimal_1_out_2_8, MAR_d_out;
  wire [7:0] alu_1_d_out, bit_extender_1_out, bit_extender_2_out, bit_extender_3_out,
       controlled_buffer_3_out, register_1_d_out;
  wire [31:0] decoder_decimal_2_out_2, decoder_decimal_3_out_2, decoder_decimal_4_out_2,
       decoder_decimal_5_out_2, decoder_decimal_6_out_2, decoder_decimal_7_out_2, decoder_decimal_8_out_2,
       decoder_decimal_9_out_2, decoder_decimal_10_out_2;

  decoder_decimal decoder_decimal_1 (
    .in_1(out_27),
    .out_2({decoder_decimal_1_out_2_8, decoder_decimal_1_out_2_7, decoder_decimal_1_out_2_6, decoder_decimal_1_out_2_5, decoder_decimal_1_out_2_4, decoder_decimal_1_out_2_3, decoder_decimal_1_out_2_2, decoder_decimal_1_out_2}));
  _7_Segment_Display u_7_segment_display_1 (
    .g(decoder_decimal_1_out_2_3[3]), .f(decoder_decimal_1_out_2_3[2]), .a(decoder_decimal_1_out_2_3[1]),
    .b(decoder_decimal_1_out_2_3[0]), .e(decoder_decimal_1_out_2_7[3]), .d(decoder_decimal_1_out_2_7[2]),
    .c(decoder_decimal_1_out_2_7[1]), .dp(decoder_decimal_1_out_2_7[0]));
  _7_Segment_Display u_7_segment_display_2 (
    .g(decoder_decimal_1_out_2_4[3]), .f(decoder_decimal_1_out_2_4[2]), .a(decoder_decimal_1_out_2_4[1]),
    .b(decoder_decimal_1_out_2_4[0]), .e(decoder_decimal_1_out_2_8[3]), .d(decoder_decimal_1_out_2_8[2]),
    .c(decoder_decimal_1_out_2_8[1]), .dp(decoder_decimal_1_out_2_8[0]));
  _7_Segment_Display u_7_segment_display_3 (
    .g(decoder_decimal_1_out_2_2[3]), .f(decoder_decimal_1_out_2_2[2]), .a(decoder_decimal_1_out_2_2[1]),
    .b(decoder_decimal_1_out_2_2[0]), .e(decoder_decimal_1_out_2_6[3]), .d(decoder_decimal_1_out_2_6[2]),
    .c(decoder_decimal_1_out_2_6[1]), .dp(decoder_decimal_1_out_2_6[0]));
  _7_Segment_Display u_7_segment_display_4 (
    .g(decoder_decimal_1_out_2[3]), .f(decoder_decimal_1_out_2[2]), .a(decoder_decimal_1_out_2[1]),
    .b(decoder_decimal_1_out_2[0]), .e(decoder_decimal_1_out_2_5[3]), .d(decoder_decimal_1_out_2_5[2]),
    .c(decoder_decimal_1_out_2_5[1]), .dp(decoder_decimal_1_out_2_5[0]));
  Clock clock_1 (.out(clock_1_out));
  decoder_decimal decoder_decimal_2 (.in_1(B), .out_2(decoder_decimal_2_out_2));
  Counter #(.width(4), .max('hf)) counter_1 (
    .D(controlled_buffer_1_out), .count(Counter_enable), .Q(Content_counter), .clk(clock_1_out));  // open: load, carry, clr
  register register_1 (
    .Clock(clock_1_out), .WE(WE_5), .Din(alu_1_d_out), .OE(OE_4), .D_out(register_1_d_out),
    .Stored_data(out_25));
  decoder_decimal decoder_decimal_3 (.in_1(A), .out_2(decoder_decimal_3_out_2));
  register register_2 (.Clock(clock_1_out), .WE(WE_7), .Din(alu_1_d_out), .Stored_data(A));  // open: OE, D_out
  ALU alu_1 (.Reg_A(A), .Reg_B(B), .OE(OE_6), .D_out(alu_1_d_out), .ALU_result(out_27));  // open: carry_out
  register register_3 (.Clock(clock_1_out), .WE(WE_8), .Din(alu_1_d_out), .Stored_data(B));  // open: OE, D_out
  _7_Segment_Display u_7_segment_display_5 (
    .g(decoder_decimal_2_out_2[15]), .f(decoder_decimal_2_out_2[14]), .a(decoder_decimal_2_out_2[13]),
    .b(decoder_decimal_2_out_2[12]), .e(decoder_decimal_2_out_2[31]), .d(decoder_decimal_2_out_2[30]),
    .c(decoder_decimal_2_out_2[29]), .dp(decoder_decimal_2_out_2[28]));
  _7_Segment_Display u_7_segment_display_6 (
    .g(decoder_decimal_2_out_2[11]), .f(decoder_decimal_2_out_2[10]), .a(decoder_decimal_2_out_2[9]),
    .b(decoder_decimal_2_out_2[8]), .e(decoder_decimal_2_out_2[27]), .d(decoder_decimal_2_out_2[26]),
    .c(decoder_decimal_2_out_2[25]), .dp(decoder_decimal_2_out_2[24]));
  assign bit_extender_1_out = {{4{1'b0}}, Content_counter};  // Bit_Extender bit_extender_1
  decoder_decimal decoder_decimal_4 (.in_1(bit_extender_1_out), .out_2(decoder_decimal_4_out_2));
  _7_Segment_Display u_7_segment_display_7 (
    .g(decoder_decimal_5_out_2[15]), .f(decoder_decimal_5_out_2[14]), .a(decoder_decimal_5_out_2[13]),
    .b(decoder_decimal_5_out_2[12]), .e(decoder_decimal_5_out_2[31]), .d(decoder_decimal_5_out_2[30]),
    .c(decoder_decimal_5_out_2[29]), .dp(decoder_decimal_5_out_2[28]));
  decoder_decimal decoder_decimal_5 (.in_1(out_25), .out_2(decoder_decimal_5_out_2));
  _7_Segment_Display u_7_segment_display_8 (
    .g(decoder_decimal_3_out_2[11]), .f(decoder_decimal_3_out_2[10]), .a(decoder_decimal_3_out_2[9]),
    .b(decoder_decimal_3_out_2[8]), .e(decoder_decimal_3_out_2[27]), .d(decoder_decimal_3_out_2[26]),
    .c(decoder_decimal_3_out_2[25]), .dp(decoder_decimal_3_out_2[24]));
  _7_Segment_Display u_7_segment_display_9 (
    .g(decoder_decimal_3_out_2[15]), .f(decoder_decimal_3_out_2[14]), .a(decoder_decimal_3_out_2[13]),
    .b(decoder_decimal_3_out_2[12]), .e(decoder_decimal_3_out_2[31]), .d(decoder_decimal_3_out_2[30]),
    .c(decoder_decimal_3_out_2[29]), .dp(decoder_decimal_3_out_2[28]));
  _7_Segment_Display u_7_segment_display_10 (
    .g(decoder_decimal_2_out_2[7]), .f(decoder_decimal_2_out_2[6]), .a(decoder_decimal_2_out_2[5]),
    .b(decoder_decimal_2_out_2[4]), .e(decoder_decimal_2_out_2[23]), .d(decoder_decimal_2_out_2[22]),
    .c(decoder_decimal_2_out_2[21]), .dp(decoder_decimal_2_out_2[20]));
  _7_Segment_Display u_7_segment_display_11 (
    .g(decoder_decimal_2_out_2[3]), .f(decoder_decimal_2_out_2[2]), .a(decoder_decimal_2_out_2[1]),
    .b(decoder_decimal_2_out_2[0]), .e(decoder_decimal_2_out_2[19]), .d(decoder_decimal_2_out_2[18]),
    .c(decoder_decimal_2_out_2[17]), .dp(decoder_decimal_2_out_2[16]));
  assign controlled_buffer_1_out = couter_oe ? Content_counter : 4'bz;  // Controlled_Buffer controlled_buffer_1
  _7_Segment_Display u_7_segment_display_12 (
    .g(decoder_decimal_4_out_2[7]), .f(decoder_decimal_4_out_2[6]), .a(decoder_decimal_4_out_2[5]),
    .b(decoder_decimal_4_out_2[4]), .e(decoder_decimal_4_out_2[23]), .d(decoder_decimal_4_out_2[22]),
    .c(decoder_decimal_4_out_2[21]), .dp(decoder_decimal_4_out_2[20]));
  _7_Segment_Display u_7_segment_display_13 (
    .g(decoder_decimal_4_out_2[3]), .f(decoder_decimal_4_out_2[2]), .a(decoder_decimal_4_out_2[1]),
    .b(decoder_decimal_4_out_2[0]), .e(decoder_decimal_4_out_2[19]), .d(decoder_decimal_4_out_2[18]),
    .c(decoder_decimal_4_out_2[17]), .dp(decoder_decimal_4_out_2[16]));
  _7_Segment_Display u_7_segment_display_14 (
    .g(decoder_decimal_5_out_2[11]), .f(decoder_decimal_5_out_2[10]), .a(decoder_decimal_5_out_2[9]),
    .b(decoder_decimal_5_out_2[8]), .e(decoder_decimal_5_out_2[27]), .d(decoder_decimal_5_out_2[26]),
    .c(decoder_decimal_5_out_2[25]), .dp(decoder_decimal_5_out_2[24]));
  _7_Segment_Display u_7_segment_display_15 (
    .g(decoder_decimal_5_out_2[7]), .f(decoder_decimal_5_out_2[6]), .a(decoder_decimal_5_out_2[5]),
    .b(decoder_decimal_5_out_2[4]), .e(decoder_decimal_5_out_2[23]), .d(decoder_decimal_5_out_2[22]),
    .c(decoder_decimal_5_out_2[21]), .dp(decoder_decimal_5_out_2[20]));
  _7_Segment_Display u_7_segment_display_16 (
    .g(decoder_decimal_3_out_2[3]), .f(decoder_decimal_3_out_2[2]), .a(decoder_decimal_3_out_2[1]),
    .b(decoder_decimal_3_out_2[0]), .e(decoder_decimal_3_out_2[19]), .d(decoder_decimal_3_out_2[18]),
    .c(decoder_decimal_3_out_2[17]), .dp(decoder_decimal_3_out_2[16]));
  _7_Segment_Display u_7_segment_display_17 (
    .g(decoder_decimal_3_out_2[7]), .f(decoder_decimal_3_out_2[6]), .a(decoder_decimal_3_out_2[5]),
    .b(decoder_decimal_3_out_2[4]), .e(decoder_decimal_3_out_2[23]), .d(decoder_decimal_3_out_2[22]),
    .c(decoder_decimal_3_out_2[21]), .dp(decoder_decimal_3_out_2[20]));
  BitSelector #(.group(4)) bitselector_1 (.in(register_1_d_out), .out(controlled_buffer_1_out), .sel(1'b0));
  _7_Segment_Display u_7_segment_display_18 (
    .g(decoder_decimal_5_out_2[3]), .f(decoder_decimal_5_out_2[2]), .a(decoder_decimal_5_out_2[1]),
    .b(decoder_decimal_5_out_2[0]), .e(decoder_decimal_5_out_2[19]), .d(decoder_decimal_5_out_2[18]),
    .c(decoder_decimal_5_out_2[17]), .dp(decoder_decimal_5_out_2[16]));
  assign alu_1_d_out = in_10 ? Testing_data : 8'bz;  // Controlled_Buffer controlled_buffer_2
  LED D7 (.in(alu_1_d_out[7]));
  LED D6 (.in(alu_1_d_out[6]));
  LED D5 (.in(alu_1_d_out[5]));
  LED D4 (.in(alu_1_d_out[4]));
  LED D3 (.in(alu_1_d_out[3]));
  LED D2 (.in(alu_1_d_out[2]));
  LED D1 (.in(alu_1_d_out[1]));
  LED D0 (.in(alu_1_d_out[0]));
  assign controlled_buffer_3_out = in_8 ? Testing_data : 8'bz;  // Controlled_Buffer controlled_buffer_3
  decoder_decimal decoder_decimal_6 (.in_1(controlled_buffer_3_out), .out_2(decoder_decimal_6_out_2));
  assign controlled_buffer_3_out = in_11 ? alu_1_d_out : 8'bz;  // Controlled_Buffer controlled_buffer_4
  _7_Segment_Display u_7_segment_display_19 (
    .g(decoder_decimal_6_out_2[11]), .f(decoder_decimal_6_out_2[10]), .a(decoder_decimal_6_out_2[9]),
    .b(decoder_decimal_6_out_2[8]), .e(decoder_decimal_6_out_2[27]), .d(decoder_decimal_6_out_2[26]),
    .c(decoder_decimal_6_out_2[25]), .dp(decoder_decimal_6_out_2[24]));
  _7_Segment_Display u_7_segment_display_20 (
    .g(decoder_decimal_6_out_2[15]), .f(decoder_decimal_6_out_2[14]), .a(decoder_decimal_6_out_2[13]),
    .b(decoder_decimal_6_out_2[12]), .e(decoder_decimal_6_out_2[31]), .d(decoder_decimal_6_out_2[30]),
    .c(decoder_decimal_6_out_2[29]), .dp(decoder_decimal_6_out_2[28]));
  _7_Segment_Display u_7_segment_display_21 (
    .g(decoder_decimal_6_out_2[3]), .f(decoder_decimal_6_out_2[2]), .a(decoder_decimal_6_out_2[1]),
    .b(decoder_decimal_6_out_2[0]), .e(decoder_decimal_6_out_2[19]), .d(decoder_decimal_6_out_2[18]),
    .c(decoder_decimal_6_out_2[17]), .dp(decoder_decimal_6_out_2[16]));
  _7_Segment_Display u_7_segment_display_22 (
    .g(decoder_decimal_6_out_2[7]), .f(decoder_decimal_6_out_2[6]), .a(decoder_decimal_6_out_2[5]),
    .b(decoder_decimal_6_out_2[4]), .e(decoder_decimal_6_out_2[23]), .d(decoder_decimal_6_out_2[22]),
    .c(decoder_decimal_6_out_2[21]), .dp(decoder_decimal_6_out_2[20]));
  MAR MAR (
    .Clock(clock_1_out), .WE(we_2), .OE(OE), .DIn(controlled_buffer_1_out), .D_out(MAR_d_out),
    .Stored_Data(Content));
  register MBR (
    .Clock(clock_1_out), .WE(WE_4), .Din(alu_1_d_out), .OE(OE_3), .D_out(alu_1_d_out), .Stored_data(out_26));
  assign alu_1_d_out = OE_internal ? out_26 : 8'bz;  // Controlled_Buffer controlled_buffer_5
  assign bit_extender_2_out = {{4{1'b0}}, Content};  // Bit_Extender bit_extender_2
  _7_Segment_Display u_7_segment_display_23 (
    .g(decoder_decimal_7_out_2[7]), .f(decoder_decimal_7_out_2[6]), .a(decoder_decimal_7_out_2[5]),
    .b(decoder_decimal_7_out_2[4]), .e(decoder_decimal_7_out_2[23]), .d(decoder_decimal_7_out_2[22]),
    .c(decoder_decimal_7_out_2[21]), .dp(decoder_decimal_7_out_2[20]));
  decoder_decimal decoder_decimal_7 (.in_1(bit_extender_2_out), .out_2(decoder_decimal_7_out_2));
  decoder_decimal decoder_decimal_8 (.in_1(out_26), .out_2(decoder_decimal_8_out_2));
  register register_4 (
    .Clock(clock_1_out), .WE(WE_6), .Din(alu_1_d_out), .OE(OE_5), .D_out(alu_1_d_out), .Stored_data(out_29));
  decoder_decimal decoder_decimal_9 (.in_1(out_29), .out_2(decoder_decimal_9_out_2));
  _7_Segment_Display u_7_segment_display_24 (
    .g(decoder_decimal_9_out_2[15]), .f(decoder_decimal_9_out_2[14]), .a(decoder_decimal_9_out_2[13]),
    .b(decoder_decimal_9_out_2[12]), .e(decoder_decimal_9_out_2[31]), .d(decoder_decimal_9_out_2[30]),
    .c(decoder_decimal_9_out_2[29]), .dp(decoder_decimal_9_out_2[28]));
  _7_Segment_Display u_7_segment_display_25 (
    .g(decoder_decimal_7_out_2[3]), .f(decoder_decimal_7_out_2[2]), .a(decoder_decimal_7_out_2[1]),
    .b(decoder_decimal_7_out_2[0]), .e(decoder_decimal_7_out_2[19]), .d(decoder_decimal_7_out_2[18]),
    .c(decoder_decimal_7_out_2[17]), .dp(decoder_decimal_7_out_2[16]));
  _7_Segment_Display u_7_segment_display_26 (
    .g(decoder_decimal_8_out_2[11]), .f(decoder_decimal_8_out_2[10]), .a(decoder_decimal_8_out_2[9]),
    .b(decoder_decimal_8_out_2[8]), .e(decoder_decimal_8_out_2[27]), .d(decoder_decimal_8_out_2[26]),
    .c(decoder_decimal_8_out_2[25]), .dp(decoder_decimal_8_out_2[24]));
  _7_Segment_Display u_7_segment_display_27 (
    .g(decoder_decimal_8_out_2[15]), .f(decoder_decimal_8_out_2[14]), .a(decoder_decimal_8_out_2[13]),
    .b(decoder_decimal_8_out_2[12]), .e(decoder_decimal_8_out_2[31]), .d(decoder_decimal_8_out_2[30]),
    .c(decoder_decimal_8_out_2[29]), .dp(decoder_decimal_8_out_2[28]));
  _7_Segment_Display u_7_segment_display_28 (
    .g(decoder_decimal_9_out_2[7]), .f(decoder_decimal_9_out_2[6]), .a(decoder_decimal_9_out_2[5]),
    .b(decoder_decimal_9_out_2[4]), .e(decoder_decimal_9_out_2[23]), .d(decoder_decimal_9_out_2[22]),
    .c(decoder_decimal_9_out_2[21]), .dp(decoder_decimal_9_out_2[20]));
  _7_Segment_Display u_7_segment_display_29 (
    .g(decoder_decimal_9_out_2[11]), .f(decoder_decimal_9_out_2[10]), .a(decoder_decimal_9_out_2[9]),
    .b(decoder_decimal_9_out_2[8]), .e(decoder_decimal_9_out_2[27]), .d(decoder_decimal_9_out_2[26]),
    .c(decoder_decimal_9_out_2[25]), .dp(decoder_decimal_9_out_2[24]));
  assign MAR_d_out = WE ? in_3 : 4'bz;  // Controlled_Buffer controlled_buffer_6
  assign bit_extender_3_out = {{4{1'b0}}, in_3};  // Bit_Extender bit_extender_3
  _7_Segment_Display u_7_segment_display_30 (
    .g(decoder_decimal_8_out_2[3]), .f(decoder_decimal_8_out_2[2]), .a(decoder_decimal_8_out_2[1]),
    .b(decoder_decimal_8_out_2[0]), .e(decoder_decimal_8_out_2[19]), .d(decoder_decimal_8_out_2[18]),
    .c(decoder_decimal_8_out_2[17]), .dp(decoder_decimal_8_out_2[16]));
  _7_Segment_Display u_7_segment_display_31 (
    .g(decoder_decimal_8_out_2[7]), .f(decoder_decimal_8_out_2[6]), .a(decoder_decimal_8_out_2[5]),
    .b(decoder_decimal_8_out_2[4]), .e(decoder_decimal_8_out_2[23]), .d(decoder_decimal_8_out_2[22]),
    .c(decoder_decimal_8_out_2[21]), .dp(decoder_decimal_8_out_2[20]));
  _7_Segment_Display u_7_segment_display_32 (
    .g(decoder_decimal_9_out_2[3]), .f(decoder_decimal_9_out_2[2]), .a(decoder_decimal_9_out_2[1]),
    .b(decoder_decimal_9_out_2[0]), .e(decoder_decimal_9_out_2[19]), .d(decoder_decimal_9_out_2[18]),
    .c(decoder_decimal_9_out_2[17]), .dp(decoder_decimal_9_out_2[16]));
  _7_Segment_Display u_7_segment_display_33 (
    .g(decoder_decimal_10_out_2[7]), .f(decoder_decimal_10_out_2[6]), .a(decoder_decimal_10_out_2[5]),
    .b(decoder_decimal_10_out_2[4]), .e(decoder_decimal_10_out_2[23]), .d(decoder_decimal_10_out_2[22]),
    .c(decoder_decimal_10_out_2[21]), .dp(decoder_decimal_10_out_2[20]));
  decoder_decimal decoder_decimal_10 (.in_1(bit_extender_3_out), .out_2(decoder_decimal_10_out_2));
  _7_Segment_Display u_7_segment_display_34 (
    .g(decoder_decimal_10_out_2[3]), .f(decoder_decimal_10_out_2[2]), .a(decoder_decimal_10_out_2[1]),
    .b(decoder_decimal_10_out_2[0]), .e(decoder_decimal_10_out_2[19]), .d(decoder_decimal_10_out_2[18]),
    .c(decoder_decimal_10_out_2[17]), .dp(decoder_decimal_10_out_2[16]));
  LED D7_2 (.in(alu_1_d_out[7]));
  LED D6_2 (.in(alu_1_d_out[6]));
  LED D5_2 (.in(alu_1_d_out[5]));
  LED D4_2 (.in(alu_1_d_out[4]));
  LED D3_2 (.in(alu_1_d_out[3]));
  LED D2_2 (.in(alu_1_d_out[2]));
  LED D1_2 (.in(alu_1_d_out[1]));
  LED D0_2 (.in(alu_1_d_out[0]));
  RAM #(.addrWidth(4), .bus("separate")) ram_1 (
    .addr(MAR_d_out), .din(alu_1_d_out), .data(alu_1_d_out), .str(WE_3), .clk(clock_1_out), .ld(OE_2));  // open: sel, clr

  // Notes on the sheet:
  //   Content ALU
  //   Intruction register
  //   Program counter
  //   ALU
  //   A content
  //   B content
  //   Internal Adress Bus
  //   Internal data bus
  //   Content MBR
  //   External Address Bus
  //   Content output register
endmodule

module cell_memory (
  input  Clock,
  input  WE,
  input  Din,
  input  EO,
  input  reset,
  output D_out,
  output Stored_data
);

  wire and_1_out, and_2_out, not_1_out, or_1_out;

  not not_1 (not_1_out, WE);
  and and_1 (and_1_out, Stored_data, not_1_out);
  and and_2 (and_2_out, WE, Din);
  or or_1 (or_1_out, and_1_out, and_2_out);
  D_Flip_Flop d_ff_1 (.clk(Clock), .D(or_1_out), .Q(Stored_data), .reset(reset));  // open: Qn, preset, en
  assign D_out = EO ? Stored_data : 1'bz;  // Controlled_Buffer controlled_buffer_1
endmodule

module register (
  input  Clock,
  input  WE,
  input  [7:0] Din,
  input  OE,
  output [7:0] D_out,
  output [7:0] Stored_data
);

  cell_memory _0 (
    .Clock(Clock), .WE(WE), .Din(Din[0]), .EO(OE), .D_out(D_out[0]), .Stored_data(Stored_data[0]));  // open: reset
  cell_memory _1 (
    .Clock(Clock), .WE(WE), .Din(Din[1]), .EO(OE), .D_out(D_out[1]), .Stored_data(Stored_data[1]));  // open: reset
  cell_memory _2 (
    .Clock(Clock), .WE(WE), .Din(Din[2]), .EO(OE), .D_out(D_out[2]), .Stored_data(Stored_data[2]));  // open: reset
  cell_memory _3 (
    .Clock(Clock), .WE(WE), .Din(Din[3]), .EO(OE), .D_out(D_out[3]), .Stored_data(Stored_data[3]));  // open: reset
  cell_memory _4 (
    .Clock(Clock), .WE(WE), .Din(Din[4]), .EO(OE), .D_out(D_out[4]), .Stored_data(Stored_data[4]));  // open: reset
  cell_memory _5 (
    .Clock(Clock), .WE(WE), .Din(Din[5]), .EO(OE), .D_out(D_out[5]), .Stored_data(Stored_data[5]));  // open: reset
  cell_memory _6 (
    .Clock(Clock), .WE(WE), .Din(Din[6]), .EO(OE), .D_out(D_out[6]), .Stored_data(Stored_data[6]));  // open: reset
  cell_memory _7 (
    .Clock(Clock), .WE(WE), .Din(Din[7]), .EO(OE), .D_out(D_out[7]), .Stored_data(Stored_data[7]));  // open: reset

  // Notes on the sheet:
  //   Registrador de 8 BITs
endmodule

module MAR (
  input  Clock,
  input  WE,
  input  OE,
  input  [3:0] DIn,
  output [3:0] D_out,
  output [3:0] Stored_Data
);

  cell_memory cell_memory_1 (
    .Clock(Clock), .WE(WE), .Din(DIn[0]), .EO(OE), .D_out(D_out[0]), .Stored_data(Stored_Data[0]));  // open: reset
  cell_memory cell_memory_2 (
    .Clock(Clock), .WE(WE), .Din(DIn[1]), .EO(OE), .D_out(D_out[1]), .Stored_data(Stored_Data[1]));  // open: reset
  cell_memory cell_memory_3 (
    .Clock(Clock), .WE(WE), .Din(DIn[2]), .EO(OE), .D_out(D_out[2]), .Stored_data(Stored_Data[2]));  // open: reset
  cell_memory cell_memory_4 (
    .Clock(Clock), .WE(WE), .Din(DIn[3]), .EO(OE), .D_out(D_out[3]), .Stored_data(Stored_Data[3]));  // open: reset
endmodule

module ALU (
  input  [7:0] Reg_A,
  input  [7:0] Reg_B,
  input  OE,
  output [7:0] D_out,
  output [7:0] ALU_result,
  output carry_out
);

  Adder adder_1 (.a(Reg_A), .b(Reg_B), .out(ALU_result), .cout(carry_out));  // open: cin
  assign D_out = OE ? ALU_result : 8'bz;  // Controlled_Buffer controlled_buffer_1

  // Notes on the sheet:
  //   Alu de 8 Bits
endmodule

// DD
module decoder_decimal (
  input  [7:0] in_1,
  output [31:0] out_2
);

  ROM #(.dataWidth(32)) rom_1 (
    .addr(in_1),
    .data({out_2[31:28], out_2[15:12], out_2[27:24], out_2[11:8], out_2[23:20], out_2[7:4], out_2[19:16], out_2[3:0]}));  // open: sel

  // Notes on the sheet:
  //   contents of rom_1 (hex, n*v repeats v):
  //   e7 21 cb 6b 2d 6e ee 23 ef 2f 21e7 2121 21cb 216b 212d 216e 21ee 2123 21ef 212f cbe7 cb21 cbcb cb6b
  //   cb2d cb6e cbee cb23 cbef cb2f 6be7 6b21 6bcb 6b6b 6b2d 6b6e 6bee 6b23 6bef 6b2f 2de7 2d21 2dcb 2d6b
  //   2d2d 2d6e 2dee 2d23 2def 2d2f 6ee7 6e21 6ecb 6e6b 6e2d 6e6e 6eee 6e23 6eef 6e2f eee7 ee21 eecb ee6b
  //   ee2d ee6e eeee ee23 eeef ee2f 23e7 2321 23cb 236b 232d 236e 23ee 2323 23ef 232f efe7 ef21 efcb ef6b
  //   ef2d ef6e efee ef23 efef ef2f 2fe7 2f21 2fcb 2f6b 2f2d 2f6e 2fee 2f23 2fef 2f2f 21e7e7 21e721 21e7cb
  //   21e76b 21e72d 21e76e 21e7ee 21e723 21e7ef 21e72f 2121e7 212121 2121cb 21216b 21212d 21216e 2121ee
  //   212123 2121ef 21212f 21cbe7 21cb21 21cbcb 21cb6b 21cb2d 21cb6e 21cbee 21cb23 21cbef 21cb2f 216be7
  //   216b21 216bcb 216b6b 216b2d 216b6e 216bee 216b23 216bef 216b2f 212de7 212d21 212dcb 212d6b 212d2d
  //   212d6e 212dee 212d23 212def 212d2f 216ee7 216e21 216ecb 216e6b 216e2d 216e6e 216eee 216e23 216eef
  //   216e2f 21eee7 21ee21 21eecb 21ee6b 21ee2d 21ee6e 21eeee 21ee23 21eeef 21ee2f 2123e7 212321 2123cb
  //   21236b 21232d 21236e 2123ee 212323 2123ef 21232f 21efe7 21ef21 21efcb 21ef6b 21ef2d 21ef6e 21efee
  //   21ef23 21efef 21ef2f 212fe7 212f21 212fcb 212f6b 212f2d 212f6e 212fee 212f23 212fef 212f2f cbe7e7
  //   cbe721 cbe7cb cbe76b cbe72d cbe76e cbe7ee cbe723 cbe7ef cbe72f cb21e7 cb2121 cb21cb cb216b cb212d
  //   cb216e cb21ee cb2123 cb21ef cb212f cbcbe7 cbcb21 cbcbcb cbcb6b cbcb2d cbcb6e cbcbee cbcb23 cbcbef
  //   cbcb2f cb6be7 cb6b21 cb6bcb cb6b6b cb6b2d cb6b6e cb6bee cb6b23 cb6bef cb6b2f cb2de7 cb2d21 cb2dcb
  //   cb2d6b cb2d2d cb2d6e cb2dee cb2d23 cb2def cb2d2f cb6ee7 cb6e21 cb6ecb cb6e6b cb6e2d cb6e6e
  //   decoder decimal
endmodule
