// Digital circuit encoder gray para binario.dig as structural Verilog
module encoder_gray_para_binario (
  input  S1,
  input  S2,
  input  S3,
  input  S4
);

  wire and_1_out, and_2_out, and_3_out, and_4_out, and_5_out, and_6_out, and_7_out, and_8_out, and_9_out,
       and_10_out, and_11_out, and_12_out, and_13_out, and_14_out, not_1_out, not_2_out, not_3_out,
       not_4_out, xor_1_out, xor_2_out, xor_3_out, xor_4_out;

  not not_1 (not_1_out, S1);
  not not_2 (not_2_out, S2);
  not not_3 (not_3_out, S3);
  not not_4 (not_4_out, S4);
  and and_1 (and_1_out, S1, S4);
  and and_2 (and_2_out, S1, S3);
  and and_3 (and_3_out, S1, S2);
  and and_4 (and_4_out, S1, not_3_out, not_4_out);
  and and_5 (and_5_out, not_1_out, S2, S4);
  and and_6 (and_6_out, not_1_out, S3, S2);
  and and_7 (and_7_out, S1, not_2_out);
  and and_8 (and_8_out, not_2_out, S3, S4);
  and and_9 (and_9_out, S2, not_4_out);
  and and_10 (and_10_out, S2, not_3_out);
  and and_11 (and_11_out, not_1_out, not_2_out, S4);
  and and_12 (and_12_out, not_1_out, not_2_out, S4);
  and and_13 (and_13_out, S4, S3);
  and and_14 (and_14_out, S2, S3);
  xor xor_1 (xor_1_out, and_12_out, and_13_out, and_14_out);
  xor xor_2 (xor_2_out, and_1_out, and_2_out, and_3_out);
  xor xor_3 (xor_3_out, and_4_out, and_5_out, and_6_out, and_7_out);
  xor xor_4 (xor_4_out, and_8_out, and_9_out, and_10_out, and_11_out);
  LED A (.in(xor_2_out));
  LED B (.in(xor_3_out));
  LED C (.in(xor_4_out));
  LED D (.in(xor_1_out));
endmodule
